// Logisim project Logisim_32bit_ALU.circ as structural Verilog: 1 circuit, main circuit main
module main (
  input  in_1,
  input  [31:0] in_2,
  input  in_3,
  input  [31:0] in_4,
  input  [3:0] in_5,
  input  in_6,
  input  [30:0] in_7,
  input  [31:0] in_8,
  output [31:0] out_9,
  output out_10
);

  wire [31:0] adder_1_out, and_1_out, or_1_out, shifter_1_out, shifter_2_out, shifter_3_out,
       subtractor_1_out, xor_1_out;
  wire [31:31] comparator_1_lt, comparator_2_lt;

  Adder #(.width(32)) adder_1 (.a(in_2), .b(in_4), .out(adder_1_out), .cin(in_1));  // open: cout
  Subtractor #(.width(32)) subtractor_1 (.a(in_2), .b(in_4), .out(subtractor_1_out), .bin(in_3));  // open: bout
  assign and_1_out = in_2 & in_4;  // AND_Gate and_1, 32 bits wide
  Comparator #(.width(32)) comparator_1 (.a(in_2), .b(in_4), .lt(comparator_1_lt[31]));  // open: gt, eq
  Comparator #(.width(32), .mode("unsigned")) comparator_2 (
    .a(in_2), .b(in_4), .lt(comparator_2_lt[31]));  // open: gt, eq
  Shifter #(.width(32)) shifter_1 (.in(in_2), .\dist (in_4[4:0]), .out(shifter_1_out));
  Shifter #(.width(32), .shift("lr")) shifter_2 (.in(in_2), .\dist (in_4[4:0]), .out(shifter_2_out));
  Shifter #(.width(32), .shift("ar")) shifter_3 (.in(in_2), .\dist (in_4[4:0]), .out(shifter_3_out));
  assign or_1_out = in_2 | in_4;  // OR_Gate or_1, 32 bits wide
  assign xor_1_out = in_2 ^ in_4;  // XOR_Gate xor_1, 32 bits wide
  Multiplexer #(.select(4), .width(32)) multiplexer_1 (
    .in0(adder_1_out), .in1(subtractor_1_out), .in2(and_1_out), .in3(or_1_out), .in4(xor_1_out),
    .in5({comparator_1_lt[31], in_7}), .in6({comparator_2_lt[31], in_7}), .in7(shifter_1_out),
    .in8(shifter_2_out), .in9(shifter_3_out), .out(out_9), .sel(in_5), .en(in_6));  // open: in10, in11, in12, in13, in14, in15
  Comparator #(.width(32)) comparator_3 (.a(out_9), .b(in_8), .eq(out_10));  // open: gt, lt
endmodule
