// Logisim project Logisim_32bit_PC_Instruction_Memory.circ as structural Verilog: 1 circuit, main circuit main
module main (
  input  reset
);

  wire clk_out;
  wire [31:0] adder_1_out, multiplexer_1_out, PC_q;

  Adder #(.width(32)) adder_1 (.a(PC_q), .b(32'h4), .out(adder_1_out));  // open: cin, cout
  Clock clk (.out(clk_out));
  Register #(.width(32)) PC (.D(adder_1_out), .Q(PC_q), .clk(clk_out), .clr(reset));  // open: en
  // Probe on PC_q
  // Probe on PC_q[3:0]
  Multiplexer #(.select(4), .width(32), .enable("false")) multiplexer_1 (
    .in0(32'ha00093), .in1({32{1'b0}}), .in2({32{1'b0}}), .in3({32{1'b0}}), .in4(32'h1400113),
    .in5({32{1'b0}}), .in6({32{1'b0}}), .in7({32{1'b0}}), .in8(32'h2081b3), .in9({32{1'b0}}),
    .in10({32{1'b0}}), .in11({32{1'b0}}), .in12(32'h302023), .in13({32{1'b0}}), .in14({32{1'b0}}),
    .in15({32{1'b0}}), .out(multiplexer_1_out), .sel(PC_q[3:0]));
  // Probe on multiplexer_1_out

  // Notes on the sheet:
  //   constant 4
  //    32 bit PC and Instruction Memory
  //   PC + 4
  //   clock (rising edge)
  //   PROGRAM COUNTER (PC)
  //   PC value goes back to the adder
  //   reset = 1 clears PC to 0
  //   addi x1, x0, 10
  //   addi x2, x0, 20
  //   add x3, x1, x2
  //   sw x3, 0(x0)
  //   memory_addr = pc[3:0]
  //   addr 0
  //   addr 1
  //   addr 2
  //   addr 3
  //   addr 4
  //   addr 5
  //   addr 6
  //   addr 7
  //   addr 8
  //   addr 9
  //   addr 10
  //   addr 11
  //   addr 12
  //   addr 13
  //   addr 14
  //   addr 15
  //   Instruction Memory (16 words x 32 bit)
endmodule
